# Fritzing sketch RemoteByWire-PiKvm (saved by Fritzing 0.9.6b)
breadboards: 1

parts:
  Nano2 = Arduino Nano v2.3
  Part3 = I2C level shifter bidirectional

nets:
  GND: Nano2.GND, Part3.GND
  N1: Nano2.D2, Part3.HV1
  N2: Nano2.+5V, Part3.HV
